# Fritzing sketch FastLEDColorControl (saved by Fritzing 0.9.3b)
breadboards: 1

parts:
  Part1 = Arduino Uno (Rev3) - ICSP
  U1 = POT [package=3362u]
  U2 = POT [package=3362u]
  U3 = POT [package=3362u]
  U4 = POT [package=3362u]
  Part2 = 12 NeoPixel Ring [part_number=1643]

nets:
  N1: Part1.A0, U1.S
  N2: Part1.A1, U2.S
  N3: Part1.A2, U3.S
  N4: Part1.A3, U4.S
  GND: Part1.GND, U1.E, U2.E, U3.E, U4.E, Part2.GND
  N5: Part1.D3_PWM, Part2.OUT
  5V: Part1.5V, U1.A, U2.A, U3.A, U4.A, Part2.VDD

custom parts:
  12 NeoPixel Ring: 12 ultra bright smart LED NeoPixels are arranged in a circle with 1.5" (37mm) outer diameter. The rings are 'chainable' - connect the output pin of one to the input pin of another. Use only one microcontroller pin to control as many as you can chain together! Each LED is addressable as the driver chip is inside the LED. Each one has ~18mA constant current drive so the color will be very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

// code stored in the sketch: FASTLEDAnalogControl.ino
//Freckledscience on a Saturday Morning
//UNO 5v  --->  Ring 5V
//UNO GND  -->  Ring GND
//UNO Pin 3 ->  Ring DI
//POT1
//  1 - GND
//  2 - A0
//  3 - 5V
//POT2
//  1 - GND
//  2 - A1
//  3 - 5V
//POT3
//  1 - GND
//  2 - A2
//  3 - 5V
//POT4
//  1 - GND
//  2 - A4
//  3 - 5V



#include <FastLED.h>


///////////////////////////////////////////////////////////////////////////////////////////
//
// Move a white dot along the strip of leds.  This program simply shows how to configure the leds,
// and then how to turn a single pixel white and then off, moving down the line of pixels.
//
#define DATA_PIN 3


// How many leds are in the strip?
#define NUM_LEDS 8
int BRIGHTNESS = 20;


#define POT1 A0
#define POT2 A1
#define POT3 A2
#define POT4 A3


// This is an array of leds.  One item for each led in your strip.
CRGB leds[NUM_LEDS];


// This function sets up the ledsand tells the controller about them
void setup() {
  // sanity check delay - allows reprogramming if accidently blowing power w/leds
  delay(2000);


  FastLED.addLeds<WS2812B, DATA_PIN, RGB>(leds, NUM_LEDS);  // GRB ordering is typical
}


// This function runs over and over, and is where you do the magic to light
// your leds.
void loop() {
  // Read all the analog inputs for potatometers
    int readBright = analogRead(POT1);
    readBright = map(readBright, 0, 1023, 0, 255);


    int RColor = analogRead(POT2);
    RColor = map(RColor, 0, 1023, 0, 255);


    int RBlue = analogRead(POT3);
    RBlue = map(RBlue, 0, 1023, 0, 255);


    int RGreen = analogRead(POT4);
    RGreen = map(RGreen, 0, 1023, 0, 255);


  //Display potatometer RGB Colors 


  for (int CLeds= 0; CLeds < NUM_LEDS; CLeds++) {
    // Turn our current led on to white, then show the leds
    leds[CLeds] = CRGB(RColor,RGreen,RBlue);
    
  }
  FastLED.setBrightness(readBright);
  FastLED.show();
  
}
